// Logisim project processor.circ as structural Verilog: 14 circuits, main circuit main
module main (
  input  in_1,
  output [4:0] rd,
  output [4:0] rs2,
  output [4:0] rs1,
  output [31:0] Instr,
  output [31:0] op1,
  output [15:0] PCOut,
  output [31:0] ALURes,
  output [31:0] op2,
  output [3:0] op,
  output [31:0] Immediate,
  output [31:0] x0,
  output [31:0] x1,
  output [31:0] x2,
  output [31:0] x5,
  output [31:0] x6,
  output [31:0] x7,
  output [31:0] x8,
  output [31:0] x9,
  output [31:0] x10
);

  wire alu_1_zero, and_1_out, clock_1_out, decode_1_alusrc, decode_1_branch, decode_1_memtoreg,
       decode_1_memwrite, decode_1_regwrite;
  wire [15:0] addr_1_sum, addr_2_sum, bitselector_1_out, bitselector_2_out, multiplexer_2_out, shifter_1_out;
  wire [31:0] datamem_1_readdata, multiplexer_3_out, regfile_1_regdata2;

  pc pc_1 (.Reset(in_1), .PCIn(multiplexer_2_out), .Clk(clock_1_out), .PCOut(PCOut));
  Clock clock_1 (.out(clock_1_out));
  instrmem instrmem_1 (.InstrAddr(PCOut), .Instr(Instr));
  decode decode_1 (
    .instr(Instr), .memwrite(decode_1_memwrite), .ALUSrc(decode_1_alusrc), .regwrite(decode_1_regwrite),
    .imm(Immediate), .memtoreg(decode_1_memtoreg), .branch(decode_1_branch), .ALUSel(op), .rd(rd), .rs1(rs1),
    .rs2(rs2));
  regfile regfile_1 (
    .WriteEn(decode_1_regwrite), .Clk(clock_1_out), .RegAddrW(rd), .RegAddr2(rs2), .RegAddr1(rs1),
    .DataIn(multiplexer_3_out), .x0(x0), .x1(x1), .x2(x2), .x5(x5), .x6(x6), .x7(x7), .x8(x8), .x9(x9),
    .x10(x10), .RegData2(regfile_1_regdata2), .RegData1(op1));
  ADDR addr_1 (.in1(PCOut), .in2(16'h1), .cin(1'b0), .sum(addr_1_sum));  // open: cout
  Multiplexer #(.width(32)) multiplexer_1 (.in0(regfile_1_regdata2), .in1(Immediate), .out(op2), .sel(decode_1_alusrc));
  BitSelector #(.group(16), .width(32)) bitselector_1 (.in(Immediate), .out(bitselector_1_out), .sel(1'b0));
  Shifter #(.shift("ar"), .width(16)) shifter_1 (.in(bitselector_1_out), .\dist (4'b0010), .out(shifter_1_out));
  alu alu_1 (.ALUSel(op), .A(op1), .B(op2), .Result(ALURes), .Zero(alu_1_zero));  // open: OverFlow
  ADDR addr_2 (.in1(PCOut), .in2(shifter_1_out), .cin(1'b0), .cout(decode_1_branch), .sum(addr_2_sum));
  and and_1 (and_1_out, decode_1_branch, alu_1_zero);
  BitSelector #(.group(16), .width(32)) bitselector_2 (.in(ALURes), .out(bitselector_2_out), .sel(1'b0));
  Multiplexer #(.width(16)) multiplexer_2 (
    .in0(addr_1_sum), .in1(addr_2_sum), .out(multiplexer_2_out), .sel(and_1_out));
  datamem datamem_1 (
    .WriteData(regfile_1_regdata2), .WriteEn(decode_1_memwrite), .Clk(clock_1_out),
    .DataAddr(bitselector_2_out), .ReadData(datamem_1_readdata));
  Multiplexer #(.width(32)) multiplexer_3 (
    .in0(datamem_1_readdata), .in1(ALURes), .out(multiplexer_3_out), .sel(decode_1_memtoreg));
endmodule

module alu (
  input  [31:0] A,
  input  [31:0] B,
  input  [3:0] ALUSel,
  output [31:0] Result,
  output Zero,
  output OverFlow
);

  wire add_1_overflow, comparator_1_eq;
  wire [4:0] bitselector_1_out;
  wire [31:0] add_1_result, and_1_out, mulh_1_out_3, mulhu_1_out_3, or_1_out, shifter_1_out, shifter_2_out,
       shifter_3_out, slt_1_result, sltu_1_result, subtractor_1_out, xor_1_out;

  BitSelector #(.group(5), .width(32)) bitselector_1 (.in(B), .out(bitselector_1_out), .sel(3'b000));
  add add_1 (.A(A), .B(B), .Result(add_1_result), .Overflow(add_1_overflow));
  Shifter #(.width(32)) shifter_1 (.in(A), .\dist (bitselector_1_out), .out(shifter_1_out));
  slt slt_1 (.A(A), .B(B), .Result(slt_1_result));
  Shifter #(.shift("lr"), .width(32)) shifter_2 (.in(A), .\dist (bitselector_1_out), .out(shifter_2_out));
  assign or_1_out = A | B;  // OR_Gate or_1, 32 bits wide
  assign and_1_out = A & B;  // AND_Gate and_1, 32 bits wide
  mul mul_1 (.A(A), .B(B));  // open: Result
  mulh mulh_1 (.in_1(A), .in_2(B), .out_3(mulh_1_out_3));
  mulhu mulhu_1 (.in_1(A), .in_2(B), .out_3(mulhu_1_out_3));
  Subtractor #(.width(32)) subtractor_1 (.a(A), .b(B), .out(subtractor_1_out), .bin(1'b0));  // open: bout
  Shifter #(.shift("ar"), .width(32)) shifter_3 (.in(A), .\dist (bitselector_1_out), .out(shifter_3_out));
  sltu sltu_1 (.A(A), .B(B), .Result(sltu_1_result));
  assign xor_1_out = A ^ B;  // XOR_Gate xor_1, 32 bits wide
  Multiplexer #(.enable("true"), .select(4), .width(32)) multiplexer_1 (
    .in0(add_1_result), .in1(shifter_1_out), .in2(slt_1_result), .in3(sltu_1_result), .in4(xor_1_out),
    .in5(shifter_2_out), .in6(or_1_out), .in7(and_1_out), .in8(subtractor_1_out), .in9(mulh_1_out_3),
    .in10({32{1'b0}}), .in11(mulhu_1_out_3), .in12(subtractor_1_out), .in13(shifter_3_out),
    .in14({32{1'b0}}), .in15(B), .out(Result), .sel(ALUSel));  // open: en
  Comparator #(.width(4)) comparator_1 (.a(ALUSel), .b(4'b0000), .eq(comparator_1_eq));  // open: gt, lt
  Comparator #(.width(32)) comparator_2 (.a(Result), .b({32{1'b0}}), .eq(Zero));  // open: gt, lt
  and and_2 (OverFlow, comparator_1_eq, add_1_overflow);
endmodule

module add (
  input  [31:0] A,
  input  [31:0] B,
  output [31:0] Result,
  output Overflow
);

  wire bitselector_1_out, bitselector_2_out, bitselector_3_out, xnor_1_out, xor_1_out;

  BitSelector #(.width(32)) bitselector_1 (.in(B), .out(bitselector_1_out), .sel({5{1'b1}}));
  BitSelector #(.width(32)) bitselector_2 (.in(A), .out(bitselector_2_out), .sel({5{1'b1}}));
  BitSelector #(.width(32)) bitselector_3 (.in(Result), .out(bitselector_3_out), .sel({5{1'b1}}));
  Adder #(.width(32)) adder_1 (.a(A), .b(B), .out(Result), .cin(1'b0));  // open: cout
  xnor xnor_1 (xnor_1_out, bitselector_1_out, bitselector_2_out);
  xor xor_1 (xor_1_out, bitselector_2_out, bitselector_3_out);
  and and_1 (Overflow, xnor_1_out, xor_1_out);
endmodule

module slt (
  input  [31:0] A,
  input  [31:0] B,
  output [31:0] Result
);

  wire comparator_1_lt;

  Comparator #(.width(32)) comparator_1 (.a(A), .b(B), .lt(comparator_1_lt));  // open: gt, eq
  assign Result = {{31{comparator_1_lt}}, comparator_1_lt};  // Bit_Extender bit_extender_1
endmodule

module mul (
  input  [31:0] A,
  input  [31:0] B,
  output [31:0] Result
);

  Multiplier #(.width(32)) multiplier_1 (.a(A), .b(B), .out(Result), .cin({32{1'b0}}));  // open: cout
endmodule

module mulh (
  input  [31:0] in_1,
  input  [31:0] in_2,
  output [31:0] out_3
);

  Multiplier #(.width(32)) multiplier_1 (.a(in_1), .b(in_2), .cin({32{1'b0}}), .cout(out_3));  // open: out
endmodule

module mulhu (
  input  [31:0] in_1,
  input  [31:0] in_2,
  output [31:0] out_3
);

  wire bitselector_1_out, bitselector_2_out;
  wire [31:0] adder_1_out, multiplexer_1_out, multiplexer_2_out, multiplier_1_cout;

  BitSelector #(.width(32)) bitselector_1 (.in(in_1), .out(bitselector_1_out), .sel({5{1'b1}}));
  BitSelector #(.width(32)) bitselector_2 (.in(in_2), .out(bitselector_2_out), .sel({5{1'b1}}));
  Multiplier #(.width(32)) multiplier_1 (.a(in_1), .b(in_2), .cin({32{1'b0}}), .cout(multiplier_1_cout));  // open: out
  Multiplexer #(.enable("true"), .width(32)) multiplexer_1 (
    .in0({32{1'b0}}), .in1(in_1), .out(multiplexer_1_out), .sel(bitselector_2_out));  // open: en
  Multiplexer #(.enable("true"), .width(32)) multiplexer_2 (
    .in0({32{1'b0}}), .in1(in_2), .out(multiplexer_2_out), .sel(bitselector_1_out));  // open: en
  Adder #(.width(32)) adder_1 (
    .a(multiplexer_1_out), .b(multiplexer_2_out), .out(adder_1_out), .cin(1'b0));  // open: cout
  Adder #(.width(32)) adder_2 (.a(multiplier_1_cout), .b(adder_1_out), .out(out_3), .cin(1'b0));  // open: cout
endmodule

module sltu (
  input  [31:0] A,
  input  [31:0] B,
  output [31:0] Result
);

  wire comparator_1_lt;

  Comparator #(.mode("unsigned"), .width(32)) comparator_1 (.a(A), .b(B), .lt(comparator_1_lt));  // open: gt, eq
  assign Result = {{31{comparator_1_lt}}, comparator_1_lt};  // Bit_Extender bit_extender_1
endmodule

module decode (
  input  [31:0] instr,
  output [4:0] rd,
  output [4:0] rs1,
  output [4:0] rs2,
  output memtoreg,
  output branch,
  output [3:0] ALUSel,
  output memwrite,
  output ALUSrc,
  output regwrite,
  output [31:0] imm
);

  wire adder_1_cout, and_1_out, bitselector_1_out, not_1_out, not_2_out, not_3_out, or_2_out;
  wire [1:0] bitselector_2_out;
  wire [3:3] or_1_out;
  wire [31:0] bit_extender_1_out, bit_extender_2_out, bit_extender_3_out;

  BitSelector #(.width(32)) bitselector_1 (.in(instr), .out(bitselector_1_out), .sel(5'b00100));
  BitSelector #(.width(32)) bitselector_2 (.in(instr), .out(bitselector_2_out[0]), .sel(5'b00101));
  BitSelector #(.width(32)) bitselector_3 (.in(instr), .out(bitselector_2_out[1]), .sel(5'b00110));
  and and_1 (and_1_out, instr[4], instr[5], instr[30]);
  assign bit_extender_1_out = {{19{instr[31]}}, {instr[31], instr[7], instr[30:25], instr[11:8], 1'b0}};  // Bit_Extender bit_extender_1
  assign bit_extender_2_out = {{20{instr[31]}}, {instr[31:25], instr[11:7]}};  // Bit_Extender bit_extender_2
  assign bit_extender_3_out = {{20{instr[31]}}, instr[31:20]};  // Bit_Extender bit_extender_3
  or or_1 (or_1_out[3], instr[6], and_1_out);
  not not_1 (not_1_out, bitselector_2_out[1]);
  not not_2 (not_2_out, bitselector_1_out);
  not not_3 (not_3_out, bitselector_2_out[0]);
  or or_2 (or_2_out, instr[4], instr[6]);
  and and_2 (memwrite, bitselector_2_out[0], not_1_out, not_2_out);
  Adder #(.width(1)) adder_1 (
    .a(bitselector_2_out[1]), .b(bitselector_2_out[0]), .cin(bitselector_1_out), .cout(adder_1_cout));  // open: out
  Multiplexer #(.width(4)) multiplexer_1 (
    .in0(4'b0000), .in1({or_1_out[3], instr[14:12]}), .out(ALUSel), .sel(or_2_out));
  or or_3 (regwrite, not_3_out, bitselector_1_out);
  Multiplexer #(.select(2), .width(32)) multiplexer_2 (
    .in0(bit_extender_3_out), .in1(bit_extender_2_out), .in2(bit_extender_1_out), .in3(bit_extender_1_out),
    .out(imm), .sel(bitselector_2_out));
  not not_4 (ALUSrc, adder_1_cout);

  assign branch = instr[6];
  assign memtoreg = instr[4];
  assign rd = instr[11:7];
  assign rs1 = instr[19:15];
  assign rs2 = instr[24:20];
endmodule

module datamem (
  input  [15:0] DataAddr,
  input  WriteEn,
  input  Clk,
  input  [31:0] WriteData,
  output [31:0] ReadData
);

  wire not_1_out;

  RAM #(.addrWidth(16), .dataWidth(32), .trigger("falling")) ram_1 (
    .addr(DataAddr), .we(WriteEn), .oe(not_1_out), .clk(Clk), .din(WriteData), .dout(ReadData));
  not not_1 (not_1_out, WriteEn);
endmodule

module instrmem (
  input  [15:0] InstrAddr,
  output [31:0] Instr
);

  ROM #(.addrWidth(16), .dataWidth(32)) rom_1 (.addr(InstrAddr), .data(Instr));

  // Notes on the sheet:
  //   contents of rom_1 (hex, n*v repeats v):
  //   500093 102223 402103
endmodule

module pc (
  input  [15:0] PCIn,
  input  Clk,
  input  Reset,
  output [15:0] PCOut
);

  Register #(.width(16)) register_1 (.D(PCIn), .en(1'b1), .clk(Clk), .Q(PCOut), .clr(Reset));
endmodule

module regfile (
  input  [4:0] RegAddr1,
  input  [31:0] DataIn,
  input  WriteEn,
  input  [4:0] RegAddrW,
  input  Clk,
  input  [4:0] RegAddr2,
  output [31:0] x0,
  output [31:0] x1,
  output [31:0] x2,
  output [31:0] x5,
  output [31:0] x6,
  output [31:0] x7,
  output [31:0] x8,
  output [31:0] x9,
  output [31:0] x10,
  output [31:0] RegData1,
  output [31:0] RegData2
);

  wire demultiplexer_1_out1, demultiplexer_1_out2, demultiplexer_1_out5, demultiplexer_1_out6,
       demultiplexer_1_out7, demultiplexer_1_out8, demultiplexer_1_out9, demultiplexer_1_out10;

  Demultiplexer #(.select(5)) demultiplexer_1 (
    .out1(demultiplexer_1_out1), .out2(demultiplexer_1_out2), .out5(demultiplexer_1_out5),
    .out6(demultiplexer_1_out6), .out7(demultiplexer_1_out7), .out8(demultiplexer_1_out8),
    .out9(demultiplexer_1_out9), .out10(demultiplexer_1_out10), .in(WriteEn), .sel(RegAddrW));  // open: out0, out3, out4, out11, out12, out13, out14, out15, out16, out17, out18, out19, out20, out21, out22, out23, out24, out25, out26, out27, out28, out29, out30, out31
  Register #(.width(32)) register_1 (.D(DataIn), .en(1'b0), .Q(x0), .clk(Clk), .clr(1'b1));
  Register #(.width(32)) register_2 (.D(DataIn), .en(demultiplexer_1_out1), .Q(x1), .clk(Clk), .clr(1'b0));
  Register #(.width(32)) register_3 (.D(DataIn), .en(demultiplexer_1_out2), .Q(x2), .clk(Clk), .clr(1'b0));
  Register #(.width(32)) register_4 (.D(DataIn), .en(demultiplexer_1_out5), .Q(x5), .clk(Clk), .clr(1'b0));
  Register #(.width(32)) register_5 (.D(DataIn), .en(demultiplexer_1_out6), .Q(x6), .clk(Clk), .clr(1'b0));
  Register #(.width(32)) register_6 (.D(DataIn), .en(demultiplexer_1_out7), .Q(x7), .clk(Clk), .clr(1'b0));
  Register #(.width(32)) register_7 (.D(DataIn), .en(demultiplexer_1_out8), .Q(x8), .clk(Clk), .clr(1'b0));
  Register #(.width(32)) register_8 (.D(DataIn), .en(demultiplexer_1_out9), .Q(x9), .clk(Clk), .clr(1'b0));
  Register #(.width(32)) register_9 (.D(DataIn), .en(demultiplexer_1_out10), .Q(x10), .clk(Clk), .clr(1'b0));
  Multiplexer #(.select(5), .width(32)) multiplexer_1 (
    .in0(x0), .in1(x1), .in2(x2), .in3({32{1'b0}}), .in4({32{1'b0}}), .in5(x5), .in6(x6), .in7(x7), .in8(x8),
    .in9(x9), .in10(x10), .in11({32{1'b0}}), .in12({32{1'b0}}), .in13({32{1'b0}}), .in14({32{1'b0}}),
    .in15({32{1'b0}}), .in16({32{1'b0}}), .in17({32{1'b0}}), .in18({32{1'b0}}), .in19({32{1'b0}}),
    .in20({32{1'b0}}), .in21({32{1'b0}}), .in22({32{1'b0}}), .in23({32{1'b0}}), .in24({32{1'b0}}),
    .in25({32{1'b0}}), .in26({32{1'b0}}), .in27({32{1'b0}}), .in28({32{1'b0}}), .in29({32{1'b0}}),
    .in30({32{1'b0}}), .in31({32{1'b0}}), .out(RegData1), .sel(RegAddr1));
  Multiplexer #(.select(5), .width(32)) multiplexer_2 (
    .in0(x0), .in1(x1), .in2(x2), .in3({32{1'b0}}), .in4({32{1'b0}}), .in5(x5), .in6(x6), .in7(x7), .in8(x8),
    .in9(x9), .in10(x10), .in11({32{1'b0}}), .in12({32{1'b0}}), .in13({32{1'b0}}), .in14({32{1'b0}}),
    .in15({32{1'b0}}), .in16({32{1'b0}}), .in17({32{1'b0}}), .in18({32{1'b0}}), .in19({32{1'b0}}),
    .in20({32{1'b0}}), .in21({32{1'b0}}), .in22({32{1'b0}}), .in23({32{1'b0}}), .in24({32{1'b0}}),
    .in25({32{1'b0}}), .in26({32{1'b0}}), .in27({32{1'b0}}), .in28({32{1'b0}}), .in29({32{1'b0}}),
    .in30({32{1'b0}}), .in31({32{1'b0}}), .out(RegData2), .sel(RegAddr2));
endmodule

module ADDR (
  input  cin,
  input  [15:0] in1,
  input  [15:0] in2,
  output [15:0] sum,
  output cout
);

  Adder #(.width(16)) adder_1 (.a(in1), .b(in2), .out(sum), .cin(cin), .cout(cout));
endmodule
